// Logisim project jaide.circ as structural Verilog: 1 circuit, main circuit main
module main (
);

  wire [1:0] sts_am;
  wire [3:0] sts_ra, sts_rb;
  wire [5:0] sts_op;
  wire [15:0] pc_q;

  Register #(.width(16)) pc (.Q(pc_q));  // open: D, en, clk, clr
  Register #(.width(16)) a ();  // open: D, en, clk, Q, clr
  Register #(.width(16)) b ();  // open: D, en, clk, Q, clr
  ROM #(.addrWidth(16), .dataWidth(16)) rom_1 (.addr(pc_q), .data({sts_op, sts_am, sts_ra, sts_rb}));
  // LedBar #(.inputtype("row"), .matrixcols(6)) ledbar_1: pin names not known; wires that end beside it: sts_op
  // LedBar #(.inputtype("row"), .matrixcols(2)) ledbar_2: pin names not known; wires that end beside it: sts_am
  // LedBar #(.inputtype("row"), .matrixcols(4)) ledbar_3: pin names not known; wires that end beside it: sts_ra
  // LedBar #(.inputtype("row"), .matrixcols(4)) ledbar_4: pin names not known; wires that end beside it: sts_rb

  // Notes on the sheet:
  //   contents of rom_1 (hex, n*v repeats v):
  //   a00 ffff
endmodule
